# Fritzing sketch activity_02 (saved by Fritzing 0.9.2b)
breadboards: 1

parts:
  Lipo_battery = LIPO-110mAh [package=lipo-110]
  R1 = Resistor [tolerance=±5% resistance=100 package=THT]
  Switch = Toggle Switch [package=THT]
  LED1 = smd LED [color="Blue (470nm)" package="1206 [SMD]"]

nets:
  N1: Lipo_battery.+, Switch.L1
  N2: Lipo_battery.-, Switch.COM, LED1.anode
  N3: R1.Pin_0, Switch.L2
  N4: R1.Pin_1, LED1.cathode
