# Fritzing sketch Act_1 circuit (saved by Fritzing 0.9.2b)
breadboards: 1

parts:
  LED = LED - 5mm [color="Blue (470nm)" package="5 mm [THT]"]
  Lipo_battery = LIPO-110mAh [package=lipo-110]
  R1 = Resistor [tolerance=±5% resistance=100 package=THT]

nets:
  N1: LED.cathode, R1.Pin_1
  N2: LED.anode, Lipo_battery.-
  N3: Lipo_battery.+, R1.Pin_0
