# Fritzing sketch Act_5 circuit (saved by Fritzing 0.9.2b)
breadboards: 1

parts:
  U1 = NodeMCU V1.0
  LED1 = smd LED [color="Blue (470nm)" package="0805 [SMD]"]
  R1 = Resistor [tolerance=±5% resistance=100 package="0402 [SMD]"]

nets:
  N1: U1.D1, U1.GND, LED1.cathode
  N2: U1.D2, R1.Pin_1
  N3: LED1.anode, R1.Pin_0

custom parts:
  NodeMCU V1.0: ESP9266 based NodeMCU
